# Fritzing sketch arcadeduino (saved by Fritzing 0.9.2b)
circuit board: 12.123cm x 4.43351cm
breadboards: 2

parts:
  R1 = Resistor [tolerance=±5% resistance=470 package=THT]
  R2 = Resistor [tolerance=±5% resistance=470 package=THT]
  R3 = Resistor [tolerance=±5% resistance=470 package=THT]
  R4 = Resistor [tolerance=±5% resistance=470 package=THT]
  R5 = Resistor [tolerance=±5% resistance=470 package=THT]
  R6 = Resistor [tolerance=±5% resistance=470 package=THT]
  R7 = Resistor [tolerance=±5% resistance=470 package=THT]
  R8 = Resistor [tolerance=±5% resistance=470 package=THT]
  R9 = Resistor [tolerance=±5% resistance=470 package=THT]
  R10 = Resistor [tolerance=±5% resistance=470 package=THT]
  R11 = Resistor [tolerance=±5% resistance=470 package=THT]
  R12 = Resistor [tolerance=±5% resistance=470 package=THT]
  R13 = Resistor [tolerance=±5% resistance=470 package=THT]
  R14 = Resistor [tolerance=±5% resistance=470 package=THT]
  R15 = Resistor [tolerance=±5% resistance=470 package=THT]
  R16 = Resistor [tolerance=±5% resistance=470 package=THT]
  R17 = Resistor [tolerance=±5% resistance=470 package=THT]
  R18 = Resistor [tolerance=±5% resistance=470 package=THT]
  R19 = Resistor [tolerance=±5% resistance=470 package=THT]
  R20 = Resistor [tolerance=±5% resistance=470 package=THT]
  R21 = Resistor [tolerance=±5% resistance=470 package=THT]
  R22 = Resistor [tolerance=±5% resistance=470 package=THT]
  R23 = Resistor [tolerance=±5% resistance=470 package=THT]
  R24 = Resistor [tolerance=±5% resistance=470 package=THT]
  J1 = female pin header, 24 pins [form="♀ (female)"]
  U3 = 74HC595 [package="DIP16 [THT]"]
  U1 = 74HC595 [package="DIP16 [THT]"]
  U2 = 74HC595 [package="DIP16 [THT]"]
  Part2 = Analog Digital MUX Breakout
  J2 = female pin header, 16 pins [form="♀ (female)"]
  Arduino1 = Arduino Pro Micro

nets:
  N1: R1.Pin_0, U1.Q0
  N2: R1.Pin_1, J1.pin1
  N3: R2.Pin_0, U1.Q1
  N4: R2.Pin_1, J1.pin2
  N5: R3.Pin_0, U1.Q3
  N6: R3.Pin_1, J1.pin4
  N7: R4.Pin_0, U1.Q2
  N8: R4.Pin_1, J1.pin3
  N9: R5.Pin_0, U1.Q6
  N10: R5.Pin_1, J1.pin7
  N11: R6.Pin_0, U1.Q4
  N12: R6.Pin_1, J1.pin5
  N13: R7.Pin_0, U1.Q7
  N14: R7.Pin_1, J1.pin8
  N15: R8.Pin_0, U1.Q5
  N16: R8.Pin_1, J1.pin6
  N17: R9.Pin_0, U2.Q0
  N18: R9.Pin_1, J1.pin9
  N19: R10.Pin_0, U2.Q1
  N20: R10.Pin_1, J1.pin10
  N21: R11.Pin_0, U2.Q2
  N22: R11.Pin_1, J1.pin11
  N23: R12.Pin_0, U2.Q6
  N24: R12.Pin_1, J1.pin15
  N25: R13.Pin_0, U2.Q4
  N26: R13.Pin_1, J1.pin13
  N27: R14.Pin_0, U2.Q5
  N28: R14.Pin_1, J1.pin14
  N29: R15.Pin_0, U2.Q3
  N30: R15.Pin_1, J1.pin12
  N31: R16.Pin_0, U2.Q7
  N32: R16.Pin_1, J1.pin16
  N33: R17.Pin_0, U3.Q0
  N34: R17.Pin_1, J1.pin17
  N35: R18.Pin_0, U3.Q1
  N36: R18.Pin_1, J1.pin18
  N37: R19.Pin_0, U3.Q2
  N38: R19.Pin_1, J1.pin19
  N39: R20.Pin_0, U3.Q6
  N40: R20.Pin_1, J1.pin23
  N41: R21.Pin_0, U3.Q4
  N42: R21.Pin_1, J1.pin21
  N43: R22.Pin_0, U3.Q5
  N44: R22.Pin_1, J1.pin22
  N45: R23.Pin_0, U3.Q3
  N46: R23.Pin_1, J1.pin20
  N47: R24.Pin_0, U3.Q7
  N48: R24.Pin_1, J1.pin24
  GND: U3.GND, U3.OE, U1.GND, U1.OE, U2.GND, U2.OE, Part2.GND, Arduino1.GND
  5V: U3.MR, U3.VCC, U1.MR, U1.VCC, U2.MR, U2.VCC, Part2.VCC, Arduino1.VCC
  N49: U3.SH_CP, U1.SH_CP, U2.SH_CP, Arduino1.D13
  N50: U3.ST_CP, U1.ST_CP, U2.ST_CP, Arduino1.D8
  N51: U3.DS, U2.Q7'
  N52: U1.Q7', U2.DS
  N53: U1.DS, Arduino1.D11_PWM
  N54: Part2.C0, J2.pin16
  N55: Part2.C1, J2.pin15
  N56: Part2.C2, J2.pin14
  N57: Part2.C3, J2.pin13
  N58: Part2.C4, J2.pin12
  N59: Part2.C5, J2.pin11
  N60: Part2.C6, J2.pin10
  N61: Part2.C7, J2.pin9
  N62: Part2.C8, J2.pin8
  N63: Part2.C9, J2.pin7
  N64: Part2.C10, J2.pin6
  N65: Part2.C11, J2.pin5
  N66: Part2.C12, J2.pin4
  N67: Part2.C13, J2.pin3
  N68: Part2.C14, J2.pin2
  N69: Part2.C15, J2.pin1
  N70: Part2.S0, Arduino1.D2
  N71: Part2.S1, Arduino1.D3_PWM
  N72: Part2.S2, Arduino1.D4
  N73: Part2.S3, Arduino1.D5_PWM
  N74: Part2.SIG, Arduino1.D6_PWM

custom parts:
  Arduino Pro Micro: The Arduino Mini is a small microcontroller board originally based on the ATmega168, but now supplied with the 328.(datasheet), intended for use on breadboards and when space is at a premium. It has 14 digital input/output pins (of which 6 can be used as PWM outputs), 8 analog inputs, and a 16 MHz crystal oscillator. It can be programmed with the USB Serial adapter or other USB or RS232 to TTL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
